// Logisim project P1.circ as structural Verilog: 17 circuits, main circuit main
module main (
);

  wire clock_1_out, cpu_1_mem_ram, cpu_1_mem_rw, not_1_out, por_1_out;
  wire [7:0] controlled_buffer_1_out, cpu_1_mem_address, cpu_1_mem_data_out, ram_1_dout, rom_1_data;

  Clock clock_1 (.out(clock_1_out));
  POR por_1 (.out(por_1_out));
  not not_1 (not_1_out, cpu_1_mem_ram);
  ROM rom_1 (.addr(cpu_1_mem_address), .data(rom_1_data));
  RAM #(.enables("line"), .trigger("falling")) ram_1 (
    .addr(cpu_1_mem_address), .we(cpu_1_mem_rw), .clk(clock_1_out), .din(cpu_1_mem_data_out),
    .dout(ram_1_dout));
  CPU cpu_1 (
    .CLK(clock_1_out), .RESET(por_1_out), .MEM_DATA_IN(controlled_buffer_1_out), .MEM_RAM(cpu_1_mem_ram),
    .MEM_RW(cpu_1_mem_rw), .MEM_ADDRESS(cpu_1_mem_address), .MEM_DATA_OUT(cpu_1_mem_data_out));
  assign controlled_buffer_1_out = not_1_out ? rom_1_data : 8'bz;  // Controlled_Buffer controlled_buffer_1
  assign controlled_buffer_1_out = cpu_1_mem_ram ? ram_1_dout : 8'bz;  // Controlled_Buffer controlled_buffer_2

  // Notes on the sheet:
  //   contents of rom_1 (hex, n*v repeats v):
  //   4e 52 d8 4d 5d d9 14 f9 31 f9 18 f9 3 f9 8 f9 17 f9 3c f9 38 f9 11 f9 4c 54 d9 9 dc c9 db 8b d2 8b
  //   d3 8b d4 7 cc 34 cc 33 f9 10 cc 27 cc 9 f9 e cc 2a cc 1 f9 8b d2 8b d3 8b d4 7 cc 34 cc 33 f9 10 cc
  //   27 cc 9 f9 e cc 2a cc 1 f9 8b d2 8b d3 8b d4 7 cc 34 cc 33 f9 10 cc 27 cc 9 f9 e cc 2a cc 1 f9 c dc
  //   8c d2 8c d3 8c d4 8c dd 8c de 8c df 9 dc 63 cc 6f f8 d9 64 cc 6e f8 cc 69 c1 cc 8c f8 d5 62 cc 6f f8
  //   d9 64 cc 6d f8 cc 69 c1 cc 8c f8 df 62 cc 6e f8 d9 63 cc 6d f8 cc 69 c1 cc 8c f8 cc 6f cc 65 c1 c1
  //   cc 4f 5c cb 90 19*0 df ce de ce cc 62 f8 dd 63 cc 6e f8 de 64 cc 6f f8 cc 6e cc 6d c0 c0 9c c8 cc 33
  //   f8 9b c8 cc 4f 5d d6 1 cb c1 d1 cb cc c0 cd cc 61 cc 1 cb c1 a6 d1 ce cc 4e 5b d7 ce b7 ce ce c8
endmodule

module OneBitAdder (
  input  A,
  input  B,
  input  C_IN,
  output S,
  output C_OUT
);

  wire and_1_out, and_2_out, xor_1_out;

  xor xor_1 (xor_1_out, A, B);
  xor xor_2 (S, xor_1_out, C_IN);
  and and_1 (and_1_out, C_IN, xor_1_out);
  and and_2 (and_2_out, A, B);
  or or_1 (C_OUT, and_1_out, and_2_out);
endmodule

// 0
module EightBitAdder (
  input  [7:0] A,
  input  [7:0] B,
  input  C_IN,
  output [7:0] S
);

  wire onebitadder_1_c_out, onebitadder_2_c_out, onebitadder_3_c_out, onebitadder_4_c_out,
       onebitadder_5_c_out, onebitadder_6_c_out, onebitadder_7_c_out;

  OneBitAdder onebitadder_1 (.A(A[0]), .B(B[0]), .C_IN(C_IN), .S(S[0]), .C_OUT(onebitadder_1_c_out));
  OneBitAdder onebitadder_2 (.A(A[1]), .B(B[1]), .C_IN(onebitadder_1_c_out), .S(S[1]), .C_OUT(onebitadder_2_c_out));
  OneBitAdder onebitadder_3 (.A(A[2]), .B(B[2]), .C_IN(onebitadder_2_c_out), .S(S[2]), .C_OUT(onebitadder_3_c_out));
  OneBitAdder onebitadder_4 (.A(A[3]), .B(B[3]), .C_IN(onebitadder_3_c_out), .S(S[3]), .C_OUT(onebitadder_4_c_out));
  OneBitAdder onebitadder_5 (.A(A[4]), .B(B[4]), .C_IN(onebitadder_4_c_out), .S(S[4]), .C_OUT(onebitadder_5_c_out));
  OneBitAdder onebitadder_6 (.A(A[5]), .B(B[5]), .C_IN(onebitadder_5_c_out), .S(S[5]), .C_OUT(onebitadder_6_c_out));
  OneBitAdder onebitadder_7 (.A(A[6]), .B(B[6]), .C_IN(onebitadder_6_c_out), .S(S[6]), .C_OUT(onebitadder_7_c_out));
  OneBitAdder onebitadder_8 (.A(A[7]), .B(B[7]), .C_IN(onebitadder_7_c_out), .S(S[7]));  // open: C_OUT
endmodule

module AddSub (
  input  [7:0] A,
  input  ControlAddSub,
  input  [7:0] B,
  output [7:0] RESULT
);

  wire [7:0] xor_1_out;

  xor xor_1 (xor_1_out[0], B[0], ControlAddSub);
  xor xor_2 (xor_1_out[1], B[1], ControlAddSub);
  xor xor_3 (xor_1_out[2], B[2], ControlAddSub);
  xor xor_4 (xor_1_out[3], B[3], ControlAddSub);
  xor xor_5 (xor_1_out[4], B[4], ControlAddSub);
  xor xor_6 (xor_1_out[5], B[5], ControlAddSub);
  xor xor_7 (xor_1_out[6], B[6], ControlAddSub);
  xor xor_8 (xor_1_out[7], B[7], ControlAddSub);
  EightBitAdder eightbitadder_1 (.A(A), .B(xor_1_out), .C_IN(ControlAddSub), .S(RESULT));
endmodule

module ALU (
  input  [3:0] OP,
  input  [7:0] X_OUT,
  input  [7:0] Y,
  output [7:0] X_IN
);

  ALUAddSub aluaddsub_1 (.OP(OP), .X_OUT(X_OUT), .Y(Y), .X_IN(X_IN));
  ALUUnaryOp aluunaryop_1 (.OP(OP), .X_OUT(X_OUT), .Y(Y), .X_IN(X_IN));
  ALUBinaryOp alubinaryop_1 (.OP(OP), .X_OUT(X_OUT), .Y(Y), .X_IN(X_IN));

  // Notes on the sheet:
  //   000 - Add
  //   001 - Sub
  //   011 - Lsh
  //   010 - Rsh
  //   100 - XOR
  //   101 - NOT
  //   110 - AND
  //   111 - OR
endmodule

module LSHRSH (
  input  LeftOrRight,
  input  [7:0] A,
  output [7:0] RESULT
);

  Multiplexer #(.width(8)) multiplexer_1 (.in0({1'b0, A[7:1]}), .in1({A[6:0], 1'b0}), .out(RESULT), .sel(LeftOrRight));
endmodule

module TheStack (
  input  [3:0] OP,
  input  CLK,
  input  RESET,
  input  [7:0] X_IN,
  output [7:0] Y_OUT,
  output [7:0] X_OUT
);

  wire and_1_out, and_2_out, and_3_out, and_4_out, and_5_out, decoder_1_out0, decoder_1_out1, decoder_1_out2,
       decoder_1_out3, decoder_1_out4, decoder_1_out5, decoder_1_out6, decoder_1_out7, not_1_out, not_2_out,
       not_3_out, not_4_out, or_1_out, or_2_out, or_3_out, or_4_out, or_5_out, or_6_out, or_7_out, or_8_out,
       or_9_out;
  wire [7:0] controlled_buffer_1_out, controlled_buffer_3_out, multiplexer_1_out, multiplexer_2_out,
       multiplexer_3_out, multiplexer_4_out, T_q, X0_q, Z_q;

  assign controlled_buffer_1_out = or_1_out ? X_IN : 8'bz;  // Controlled_Buffer controlled_buffer_1
  and and_1 (and_1_out, OP[3], or_4_out);
  and and_2 (and_2_out, OP[3], not_3_out);
  and and_3 (and_3_out, OP[3], not_1_out);
  Decoder #(.select(3)) decoder_1 (
    .out0(decoder_1_out0), .out1(decoder_1_out1), .out2(decoder_1_out2), .out3(decoder_1_out3),
    .out4(decoder_1_out4), .out5(decoder_1_out5), .out6(decoder_1_out6), .out7(decoder_1_out7), .sel(OP[2:0]));  // open: en
  and and_4 (and_4_out, OP[3], not_2_out);
  and and_5 (and_5_out, OP[3], or_7_out);
  or or_1 (or_1_out, decoder_1_out0, decoder_1_out1, decoder_1_out2);
  or or_2 (or_2_out, decoder_1_out0, decoder_1_out1);
  not not_1 (not_1_out, or_2_out);
  or or_3 (or_3_out, or_2_out, decoder_1_out3);
  not not_2 (not_2_out, or_3_out);
  or or_4 (or_4_out, decoder_1_out1, decoder_1_out2);
  not not_3 (not_3_out, decoder_1_out4);
  or or_5 (or_5_out, decoder_1_out3, or_6_out);
  or or_6 (or_6_out, decoder_1_out4, decoder_1_out5);
  or or_7 (or_7_out, or_6_out, decoder_1_out7);
  or or_8 (or_8_out, decoder_1_out6, decoder_1_out7);
  or or_9 (or_9_out, or_8_out, decoder_1_out3);
  not not_4 (not_4_out, or_9_out);
  Register T (.D(multiplexer_1_out), .en(and_5_out), .clk(CLK), .Q(T_q), .clr(RESET));
  Multiplexer #(.width(8)) multiplexer_1 (
    .in0(X_OUT), .in1(controlled_buffer_3_out), .out(multiplexer_1_out), .sel(or_6_out));
  Register Z (.D(multiplexer_2_out), .en(and_4_out), .clk(CLK), .Q(Z_q), .clr(RESET));
  Multiplexer #(.width(8)) multiplexer_2 (.in0(T_q), .in1(Y_OUT), .out(multiplexer_2_out), .sel(or_6_out));
  Register Y (.D(multiplexer_3_out), .en(and_3_out), .clk(CLK), .Q(Y_OUT), .clr(RESET));
  Multiplexer #(.width(8)) multiplexer_3 (
    .in0(controlled_buffer_3_out), .in1(X_OUT), .out(multiplexer_3_out), .sel(or_5_out));
  Register X (.D(multiplexer_4_out), .en(and_2_out), .clk(CLK), .Q(X_OUT), .clr(RESET));
  Multiplexer #(.width(8)) multiplexer_4 (
    .in0(Y_OUT), .in1(controlled_buffer_1_out), .out(multiplexer_4_out), .sel(not_4_out));
  Register X0 (.D(X_OUT), .en(and_1_out), .clk(CLK), .Q(X0_q), .clr(RESET));
  assign controlled_buffer_1_out = or_8_out ? T_q : 8'bz;  // Controlled_Buffer controlled_buffer_2
  assign controlled_buffer_3_out = and_4_out ? Z_q : 8'bz;  // Controlled_Buffer controlled_buffer_3
  assign controlled_buffer_1_out = decoder_1_out5 ? X0_q : 8'bz;  // Controlled_Buffer controlled_buffer_4

  // Notes on the sheet:
  //   1000 - LOAD
  //   1001 -  ALU_UN
  //   1010 - ALU_BIN
  //   1011 - EXY
  //   1100 - PTS
  //   1101 - RPV
  //   1110 - POP
  //   1111 - RTS
  //   Remove this gate in implementation
  //   LOAD
  //   ALU_UN
  //   ALU_BIN
  //   EXY
  //   PTS
  //   RPV
  //   POP
  //   RTS
endmodule

module RegisterFile (
  input  CLK,
  input  RESET,
  input  [3:0] REGISTER_ID,
  input  WVR,
  input  INDIRECT_OP,
  input  RVR,
  input  [7:0] X_OUT,
  input  [7:0] Y_OUT,
  output [7:0] ADDRESS_OUT,
  output [7:0] X_IN
);

  wire and_1_out, and_2_out, and_3_out, and_4_out, and_5_out, and_6_out, decoder_1_out1, decoder_1_out2,
       decoder_1_out3, decoder_1_out4, decoder_1_out5, decoder_1_out6, decoder_1_out7, decoder_1_out8,
       decoder_1_out9, decoder_1_out10, decoder_1_out11, decoder_1_out12, decoder_1_out13, decoder_1_out14,
       decoder_1_out15, decoder_2_out0, decoder_2_out1, decoder_2_out2, decoder_2_out3, decoder_2_out4,
       decoder_2_out5, decoder_2_out6, decoder_2_out7, decoder_2_out8, decoder_2_out9, decoder_2_out10,
       decoder_2_out11, decoder_2_out12, decoder_2_out13, decoder_2_out14, decoder_2_out15, not_1_out,
       not_2_out, not_3_out, or_1_out, or_2_out, or_3_out, or_4_out, or_5_out;
  wire [7:0] addsub_1_result, multiplexer_1_out, R1_q, R2_q, R3_q, R4_q, R5_q, R6_q, R7_q, R8_q, R9_q, R10_q,
       R11_q, R12_q, R13_q, R14_q, R15_q;

  not not_1 (not_1_out, REGISTER_ID[3]);
  not not_2 (not_2_out, REGISTER_ID[2]);
  Multiplexer #(.width(8)) multiplexer_1 (
    .in0(X_OUT), .in1(addsub_1_result), .out(multiplexer_1_out), .sel(INDIRECT_OP));
  not not_3 (not_3_out, REGISTER_ID[1]);
  and and_1 (and_1_out, not_1_out, not_2_out, REGISTER_ID[0]);
  and and_2 (and_2_out, not_1_out, not_2_out, REGISTER_ID[1]);
  and and_3 (and_3_out, not_1_out, REGISTER_ID[2], not_3_out);
  and and_4 (and_4_out, REGISTER_ID[3], REGISTER_ID[2]);
  and and_5 (and_5_out, REGISTER_ID[3], REGISTER_ID[1], REGISTER_ID[0]);
  or or_1 (or_1_out, and_4_out, and_5_out);
  or or_2 (or_2_out, and_1_out, and_2_out, and_3_out);
  or or_3 (or_3_out, or_1_out, or_2_out);
  and and_6 (and_6_out, or_3_out, INDIRECT_OP);
  or or_4 (or_4_out, WVR, and_6_out);
  Decoder #(.select(4)) decoder_1 (
    .out1(decoder_1_out1), .out2(decoder_1_out2), .out3(decoder_1_out3), .out4(decoder_1_out4),
    .out5(decoder_1_out5), .out6(decoder_1_out6), .out7(decoder_1_out7), .out8(decoder_1_out8),
    .out9(decoder_1_out9), .out10(decoder_1_out10), .out11(decoder_1_out11), .out12(decoder_1_out12),
    .out13(decoder_1_out13), .out14(decoder_1_out14), .out15(decoder_1_out15), .sel(REGISTER_ID),
    .en(or_4_out));  // open: out0
  or or_5 (or_5_out, RVR, INDIRECT_OP);
  Decoder #(.select(4)) decoder_2 (
    .out0(decoder_2_out0), .out1(decoder_2_out1), .out2(decoder_2_out2), .out3(decoder_2_out3),
    .out4(decoder_2_out4), .out5(decoder_2_out5), .out6(decoder_2_out6), .out7(decoder_2_out7),
    .out8(decoder_2_out8), .out9(decoder_2_out9), .out10(decoder_2_out10), .out11(decoder_2_out11),
    .out12(decoder_2_out12), .out13(decoder_2_out13), .out14(decoder_2_out14), .out15(decoder_2_out15),
    .sel(REGISTER_ID), .en(or_5_out));
  Register R1 (.D(multiplexer_1_out), .en(decoder_1_out1), .clk(CLK), .Q(R1_q), .clr(RESET));
  Register R2 (.D(multiplexer_1_out), .en(decoder_1_out2), .clk(CLK), .Q(R2_q), .clr(RESET));
  Register R3 (.D(multiplexer_1_out), .en(decoder_1_out3), .clk(CLK), .Q(R3_q), .clr(RESET));
  Register R4 (.D(multiplexer_1_out), .en(decoder_1_out4), .clk(CLK), .Q(R4_q), .clr(RESET));
  Register R5 (.D(multiplexer_1_out), .en(decoder_1_out5), .clk(CLK), .Q(R5_q), .clr(RESET));
  Register R6 (.D(multiplexer_1_out), .en(decoder_1_out6), .clk(CLK), .Q(R6_q), .clr(RESET));
  Register R7 (.D(multiplexer_1_out), .en(decoder_1_out7), .clk(CLK), .Q(R7_q), .clr(RESET));
  Register R8 (.D(multiplexer_1_out), .en(decoder_1_out8), .clk(CLK), .Q(R8_q), .clr(RESET));
  Register R9 (.D(multiplexer_1_out), .en(decoder_1_out9), .clk(CLK), .Q(R9_q), .clr(RESET));
  Register R10 (.D(multiplexer_1_out), .en(decoder_1_out10), .clk(CLK), .Q(R10_q), .clr(RESET));
  Register R11 (.D(multiplexer_1_out), .en(decoder_1_out11), .clk(CLK), .Q(R11_q), .clr(RESET));
  Register R12 (.D(multiplexer_1_out), .en(decoder_1_out12), .clk(CLK), .Q(R12_q), .clr(RESET));
  Register R13 (.D(multiplexer_1_out), .en(decoder_1_out13), .clk(CLK), .Q(R13_q), .clr(RESET));
  Register R14 (.D(multiplexer_1_out), .en(decoder_1_out14), .clk(CLK), .Q(R14_q), .clr(RESET));
  Register R15 (.D(multiplexer_1_out), .en(decoder_1_out15), .clk(CLK), .Q(R15_q), .clr(RESET));
  assign ADDRESS_OUT = decoder_2_out1 ? R1_q : 8'bz;  // Controlled_Buffer controlled_buffer_1
  assign ADDRESS_OUT = decoder_2_out2 ? R2_q : 8'bz;  // Controlled_Buffer controlled_buffer_2
  assign ADDRESS_OUT = decoder_2_out3 ? R3_q : 8'bz;  // Controlled_Buffer controlled_buffer_3
  assign ADDRESS_OUT = decoder_2_out4 ? R4_q : 8'bz;  // Controlled_Buffer controlled_buffer_4
  assign ADDRESS_OUT = decoder_2_out5 ? R5_q : 8'bz;  // Controlled_Buffer controlled_buffer_5
  assign ADDRESS_OUT = decoder_2_out6 ? R6_q : 8'bz;  // Controlled_Buffer controlled_buffer_6
  assign ADDRESS_OUT = decoder_2_out7 ? R7_q : 8'bz;  // Controlled_Buffer controlled_buffer_7
  assign ADDRESS_OUT = decoder_2_out8 ? R8_q : 8'bz;  // Controlled_Buffer controlled_buffer_8
  assign ADDRESS_OUT = decoder_2_out9 ? R9_q : 8'bz;  // Controlled_Buffer controlled_buffer_9
  assign ADDRESS_OUT = decoder_2_out10 ? R10_q : 8'bz;  // Controlled_Buffer controlled_buffer_10
  assign ADDRESS_OUT = decoder_2_out11 ? R11_q : 8'bz;  // Controlled_Buffer controlled_buffer_11
  assign ADDRESS_OUT = decoder_2_out12 ? R12_q : 8'bz;  // Controlled_Buffer controlled_buffer_12
  assign ADDRESS_OUT = decoder_2_out13 ? R13_q : 8'bz;  // Controlled_Buffer controlled_buffer_13
  assign ADDRESS_OUT = decoder_2_out14 ? R14_q : 8'bz;  // Controlled_Buffer controlled_buffer_14
  assign ADDRESS_OUT = decoder_2_out15 ? R15_q : 8'bz;  // Controlled_Buffer controlled_buffer_15
  assign ADDRESS_OUT = decoder_2_out0 ? Y_OUT : 8'bz;  // Controlled_Buffer controlled_buffer_16
  AddSub addsub_1 (.A(ADDRESS_OUT), .ControlAddSub(or_2_out), .B(8'h1), .RESULT(addsub_1_result));

  assign X_IN = ADDRESS_OUT;
endmodule

module CPU (
  input  CLK,
  input  RESET,
  input  [7:0] MEM_DATA_IN,
  output MEM_RAM,
  output MEM_RW,
  output [7:0] MEM_ADDRESS,
  output [7:0] MEM_DATA_OUT
);

  wire callstack_1_error, instructiondecoder_1_call, instructiondecoder_1_indirect_op,
       instructiondecoder_1_mem_op_data, instructiondecoder_1_mem_op_rw, instructiondecoder_1_ret,
       instructiondecoder_1_rvr, instructiondecoder_1_set_pc, instructiondecoder_1_wvr;
  wire [3:0] instructiondecoder_1_alu_op, instructiondecoder_1_register_id, instructiondecoder_1_stackop;
  wire [7:0] fetch_1_op_address, fetch_1_opcode, memoryinterface_1_instruction, registerfile_1_address_out,
       registerfile_1_x_in, thestack_1_x_out, thestack_1_y_out;

  TheStack thestack_1 (
    .OP(instructiondecoder_1_stackop), .CLK(CLK), .RESET(RESET), .X_IN(registerfile_1_x_in),
    .Y_OUT(thestack_1_y_out), .X_OUT(thestack_1_x_out));
  RegisterFile registerfile_1 (
    .CLK(CLK), .RESET(RESET), .REGISTER_ID(instructiondecoder_1_register_id), .WVR(instructiondecoder_1_wvr),
    .INDIRECT_OP(instructiondecoder_1_indirect_op), .RVR(instructiondecoder_1_rvr), .X_OUT(thestack_1_x_out),
    .Y_OUT(thestack_1_y_out), .ADDRESS_OUT(registerfile_1_address_out), .X_IN(registerfile_1_x_in));
  ALU alu_1 (
    .OP(instructiondecoder_1_alu_op), .X_OUT(thestack_1_x_out), .Y(thestack_1_y_out),
    .X_IN(registerfile_1_x_in));
  CallStack callstack_1 (
    .CLOCK(CLK), .RESET(RESET), .CALL(instructiondecoder_1_call), .RET(instructiondecoder_1_ret),
    .NEXT_ADDRESS(fetch_1_op_address), .ERROR(callstack_1_error), .ADDRESS_OUT(registerfile_1_address_out));
  Fetch fetch_1 (
    .CLOCK(CLK), .RESET(RESET), .ERROR(callstack_1_error), .MEM_OP_DATA(instructiondecoder_1_mem_op_rw),
    .INSTRUCTION(memoryinterface_1_instruction), .SET_PC(instructiondecoder_1_set_pc),
    .ADDRESS_IN(registerfile_1_address_out), .OP_ADDRESS(fetch_1_op_address), .OPCODE(fetch_1_opcode));
  MemoryInterface memoryinterface_1 (
    .MEM_OP_DATA(instructiondecoder_1_mem_op_data), .MEM_OP_RW(instructiondecoder_1_mem_op_rw),
    .OP_ADDRESS(fetch_1_op_address), .DATA_ADDRESS(registerfile_1_address_out), .X_OUT(thestack_1_x_out),
    .MEM_DATA_IN(MEM_DATA_IN), .INSTRUCTION(memoryinterface_1_instruction), .X_IN(registerfile_1_x_in),
    .MEM_RAM(MEM_RAM), .MEM_RW(MEM_RW), .MEM_ADDRESS(MEM_ADDRESS), .MEM_DATA_OUT(MEM_DATA_OUT));
  InstructionDecoder instructiondecoder_1 (
    .OPCODE(fetch_1_opcode), .X_OUT(thestack_1_x_out), .ALU_OP(instructiondecoder_1_alu_op),
    .StackOp(instructiondecoder_1_stackop), .RET(instructiondecoder_1_ret),
    .REGISTER_ID(instructiondecoder_1_register_id), .X_IN(registerfile_1_x_in),
    .INDIRECT_OP(instructiondecoder_1_indirect_op), .CALL(instructiondecoder_1_call),
    .SET_PC(instructiondecoder_1_set_pc), .WVR(instructiondecoder_1_wvr), .RVR(instructiondecoder_1_rvr),
    .MEM_OP_RW(instructiondecoder_1_mem_op_rw), .MEM_OP_DATA(instructiondecoder_1_mem_op_data));
endmodule

module MemoryInterface (
  input  MEM_OP_DATA,
  input  MEM_OP_RW,
  input  [7:0] OP_ADDRESS,
  input  [7:0] DATA_ADDRESS,
  input  [7:0] X_OUT,
  input  [7:0] MEM_DATA_IN,
  output [7:0] INSTRUCTION,
  output [7:0] X_IN,
  output MEM_RAM,
  output MEM_RW,
  output [7:0] MEM_ADDRESS,
  output [7:0] MEM_DATA_OUT
);

  wire and_1_out, not_1_out, not_2_out;

  Multiplexer #(.width(8)) multiplexer_1 (.in0(OP_ADDRESS), .in1(DATA_ADDRESS), .out(MEM_ADDRESS), .sel(MEM_OP_DATA));
  not not_1 (not_1_out, MEM_OP_RW);
  assign MEM_DATA_OUT = MEM_RW ? X_OUT : 8'bz;  // Controlled_Buffer controlled_buffer_1
  assign INSTRUCTION = not_2_out ? MEM_DATA_IN : 8'bz;  // Controlled_Buffer controlled_buffer_2
  and and_1 (and_1_out, MEM_OP_DATA, not_1_out);
  not not_2 (not_2_out, MEM_RW);
  and and_2 (MEM_RW, MEM_OP_DATA, MEM_OP_RW);
  assign X_IN = and_1_out ? INSTRUCTION : 8'bz;  // Controlled_Buffer controlled_buffer_3

  assign MEM_RAM = MEM_OP_DATA;

  // Notes on the sheet:
  //   Remove in physical implementation and replace with a transciever
endmodule

module Fetch (
  input  CLOCK,
  input  RESET,
  input  ERROR,
  input  MEM_OP_DATA,
  input  [7:0] INSTRUCTION,
  input  SET_PC,
  input  [7:0] ADDRESS_IN,
  output [7:0] OP_ADDRESS,
  output [7:0] OPCODE
);

  wire ERROR_LATCH_q, or_1_out, or_2_out, or_3_out;
  wire [7:0] eightbitadder_1_s, multiplexer_1_out, multiplexer_2_out, multiplexer_3_out;

  Register #(.width(1)) ERROR_LATCH (.D(1'b1), .en(ERROR), .clk(CLOCK), .Q(ERROR_LATCH_q), .clr(RESET));
  or or_1 (or_1_out, or_2_out, SET_PC);
  Multiplexer #(.width(8)) multiplexer_1 (.in0(INSTRUCTION), .in1({8{1'b0}}), .out(multiplexer_1_out), .sel(or_1_out));
  or or_2 (or_2_out, ERROR_LATCH_q, MEM_OP_DATA);
  or or_3 (or_3_out, or_2_out, SET_PC);
  Multiplexer #(.width(8)) multiplexer_2 (.in0(OP_ADDRESS), .in1(ADDRESS_IN), .out(multiplexer_2_out), .sel(SET_PC));
  Multiplexer #(.width(8)) multiplexer_3 (
    .in0(eightbitadder_1_s), .in1(multiplexer_2_out), .out(multiplexer_3_out), .sel(or_3_out));
  Register PC (.D(multiplexer_3_out), .en(1'b1), .clk(CLOCK), .Q(OP_ADDRESS), .clr(RESET));
  Register OP (.D(multiplexer_1_out), .en(1'b1), .clk(CLOCK), .Q(OPCODE), .clr(RESET));
  EightBitAdder eightbitadder_1 (.A(OP_ADDRESS), .B(8'h1), .C_IN(1'b0), .S(eightbitadder_1_s));
endmodule

module BranchUnit (
  input  JMP,
  input  JGT,
  input  JZ,
  input  [7:0] X_OUT,
  output BRANCH_TAKEN
);

  wire and_1_out, and_2_out, nor_1_out, not_1_out, or_1_out;

  nor nor_1 (nor_1_out, X_OUT[0], X_OUT[1], X_OUT[2], X_OUT[3], X_OUT[4], X_OUT[5], X_OUT[6], X_OUT[7]);
  and and_1 (and_1_out, JZ, nor_1_out);
  not not_1 (not_1_out, X_OUT[7]);
  and and_2 (and_2_out, not_1_out, JGT);
  or or_1 (or_1_out, and_2_out, and_1_out);
  or or_2 (BRANCH_TAKEN, JMP, or_1_out);
endmodule

module CallStack (
  input  CLOCK,
  input  RESET,
  input  CALL,
  input  RET,
  input  [7:0] NEXT_ADDRESS,
  output ERROR,
  output [7:0] ADDRESS_OUT
);

  wire and_1_out, and_2_out, and_3_out, decoder_1_out0, decoder_1_out1, decoder_1_out2, decoder_1_out3,
       decoder_2_out0, decoder_2_out1, decoder_2_out2, decoder_2_out3, not_1_out, or_1_out;
  wire [1:0] addsub_1_result, STATE_q;
  wire [7:0] S0_q, S1_q, S2_q, S3_q;
  wire [7:2] addsub_1_result_2, STATE_q_2;

  Decoder #(.select(2)) decoder_1 (
    .out0(decoder_1_out0), .out1(decoder_1_out1), .out2(decoder_1_out2), .out3(decoder_1_out3),
    .sel(STATE_q), .en(CALL));
  or or_1 (or_1_out, CALL, RET);
  Register S0 (.D(NEXT_ADDRESS), .en(decoder_1_out0), .clk(CLOCK), .Q(S0_q), .clr(RESET));
  Register S1 (.D(NEXT_ADDRESS), .en(decoder_1_out1), .clk(CLOCK), .Q(S1_q), .clr(RESET));
  Register S2 (.D(NEXT_ADDRESS), .en(decoder_1_out2), .clk(CLOCK), .Q(S2_q), .clr(RESET));
  Register S3 (.D(NEXT_ADDRESS), .en(decoder_1_out3), .clk(CLOCK), .Q(S3_q), .clr(RESET));
  Decoder #(.select(2)) decoder_2 (
    .out0(decoder_2_out0), .out1(decoder_2_out1), .out2(decoder_2_out2), .out3(decoder_2_out3),
    .sel(addsub_1_result), .en(RET));
  Register STATE (
    .D({addsub_1_result_2, addsub_1_result}), .en(or_1_out), .clk(CLOCK), .Q({STATE_q_2, STATE_q}),
    .clr(RESET));
  assign ADDRESS_OUT = decoder_2_out0 ? S0_q : 8'bz;  // Controlled_Buffer controlled_buffer_1
  assign ADDRESS_OUT = decoder_2_out1 ? S1_q : 8'bz;  // Controlled_Buffer controlled_buffer_2
  assign ADDRESS_OUT = decoder_2_out2 ? S2_q : 8'bz;  // Controlled_Buffer controlled_buffer_3
  assign ADDRESS_OUT = decoder_2_out3 ? S3_q : 8'bz;  // Controlled_Buffer controlled_buffer_4
  not not_1 (not_1_out, STATE_q[1]);
  and and_1 (and_1_out, STATE_q[0], not_1_out, STATE_q_2[2], CALL);
  and and_2 (and_2_out, STATE_q[0], STATE_q[1], STATE_q_2[2], STATE_q_2[3], STATE_q_2[4], STATE_q_2[5], STATE_q_2[6], STATE_q_2[7]);
  AddSub addsub_1 (
    .A({STATE_q_2, STATE_q}), .ControlAddSub(RET), .B(8'h1), .RESULT({addsub_1_result_2, addsub_1_result}));
  and and_3 (and_3_out, and_2_out, RET);
  or or_2 (ERROR, and_1_out, and_3_out);
endmodule

module InstructionDecoder (
  input  [7:0] OPCODE,
  input  [7:0] X_OUT,
  output [3:0] ALU_OP,
  output [3:0] StackOp,
  output RET,
  output [3:0] REGISTER_ID,
  output [7:0] X_IN,
  output INDIRECT_OP,
  output CALL,
  output SET_PC,
  output WVR,
  output RVR,
  output MEM_OP_RW,
  output MEM_OP_DATA
);

  wire and_1_out, and_3_out, and_4_out, and_6_out, and_7_out, and_8_out, and_11_out, BIN_OP_out,
       branchunit_1_branch_taken, CLR_out, LD_out, LUP_PUP_out, nor_1_out, nor_2_out, not_1_out, not_2_out,
       not_3_out, not_4_out, not_5_out, not_6_out, not_7_out, not_8_out, not_9_out, not_10_out, not_11_out,
       not_12_out, not_13_out, not_14_out, or_1_out, or_2_out, or_3_out, or_4_out, or_6_out, or_8_out,
       SHORT_IMM_out, STACK_OP_out, STACK_OP_PREFIX_out, UN_OP_out;
  wire [2:0] priority_encoder_1_out;
  wire [3:3] or_5_out;
  wire [7:0] multiplexer_1_out, multiplexer_3_out, multiplexer_4_out;

  not not_1 (not_1_out, OPCODE[5]);
  not not_2 (not_2_out, OPCODE[5]);
  not not_3 (not_3_out, OPCODE[3]);
  not not_4 (not_4_out, OPCODE[4]);
  not not_5 (not_5_out, OPCODE[2]);
  not not_6 (not_6_out, OPCODE[4]);
  not not_7 (not_7_out, OPCODE[1]);
  nor SHORT_IMM (SHORT_IMM_out, OPCODE[6], OPCODE[7]);
  or or_1 (or_1_out, OPCODE[0], OPCODE[1], OPCODE[2], OPCODE[3], OPCODE[4], OPCODE[5], OPCODE[6], OPCODE[7]);
  and and_1 (and_1_out, SHORT_IMM_out, or_1_out);
  not not_8 (not_8_out, OPCODE[5]);
  not not_9 (not_9_out, OPCODE[7]);
  not not_10 (not_10_out, OPCODE[4]);
  not not_11 (not_11_out, OPCODE[6]);
  not not_12 (not_12_out, OPCODE[5]);
  not not_13 (not_13_out, OPCODE[7]);
  and and_2 (ALU_OP[3], not_3_out, not_4_out, not_1_out, OPCODE[6], OPCODE[7]);
  and and_3 (and_3_out, not_5_out, OPCODE[1]);
  and and_4 (and_4_out, OPCODE[2], not_7_out, OPCODE[0]);
  and STACK_OP_PREFIX (STACK_OP_PREFIX_out, OPCODE[3], not_6_out, not_2_out, OPCODE[6], OPCODE[7]);
  nor nor_1 (nor_1_out, OPCODE[0], OPCODE[1], OPCODE[2]);
  nor nor_2 (nor_2_out, OPCODE[1], OPCODE[2]);
  and LUP_PUP (LUP_PUP_out, not_8_out, OPCODE[6], not_9_out);
  or or_2 (or_2_out, and_3_out, and_4_out);
  and CLR (CLR_out, STACK_OP_PREFIX_out, OPCODE[0], nor_2_out);
  and and_5 (CALL, OPCODE[4], OPCODE[5], OPCODE[6], OPCODE[7]);
  and and_6 (and_6_out, not_10_out, OPCODE[5], OPCODE[6], OPCODE[7]);
  and and_7 (and_7_out, OPCODE[4], OPCODE[5], not_11_out, OPCODE[7]);
  and and_8 (and_8_out, not_10_out, OPCODE[5], not_11_out, OPCODE[7]);
  and and_9 (WVR, OPCODE[4], not_12_out, OPCODE[6], OPCODE[7]);
  and and_10 (RVR, not_10_out, OPCODE[5], OPCODE[6], not_13_out);
  and ST (MEM_OP_RW, OPCODE[4], not_12_out, not_11_out, OPCODE[7]);
  and LD (LD_out, not_10_out, not_12_out, not_11_out, OPCODE[7]);
  not not_14 (not_14_out, or_2_out);
  and and_11 (and_11_out, OPCODE[0], OPCODE[1]);
  and and_12 (RET, STACK_OP_PREFIX_out, nor_1_out);
  or or_3 (or_3_out, and_11_out, OPCODE[2]);
  and UN_OP (UN_OP_out, ALU_OP[3], or_2_out);
  and BIN_OP (BIN_OP_out, ALU_OP[3], not_14_out);
  and STACK_OP (STACK_OP_out, or_3_out, STACK_OP_PREFIX_out);
  or or_4 (or_4_out, or_8_out, RVR, LD_out);
  Multiplexer #(.width(8)) multiplexer_1 (
    .in0({OPCODE[3:0], X_OUT[3:0]}), .in1({X_OUT[7:4], OPCODE[3:0]}), .out(multiplexer_1_out), .sel(OPCODE[4]));
  Priority_Encoder priority_encoder_1 (
    .in0(or_4_out), .in1(UN_OP_out), .in2(BIN_OP_out), .out(priority_encoder_1_out));  // open: in3, in4, in5, in6, in7, en_in, gs, en_out
  or or_5 (or_5_out[3], or_4_out, UN_OP_out, BIN_OP_out);
  BranchUnit branchunit_1 (
    .JMP(and_7_out), .JGT(and_6_out), .JZ(and_8_out), .X_OUT(X_OUT), .BRANCH_TAKEN(branchunit_1_branch_taken));
  Multiplexer #(.width(4)) multiplexer_2 (
    .in0({or_5_out[3], priority_encoder_1_out}), .in1(OPCODE[3:0]), .out(StackOp), .sel(STACK_OP_out));
  Multiplexer #(.width(8)) multiplexer_3 (
    .in0(OPCODE), .in1(multiplexer_1_out), .out(multiplexer_3_out), .sel(LUP_PUP_out));
  Multiplexer #(.width(8)) multiplexer_4 (
    .in0({8{1'b0}}), .in1(multiplexer_3_out), .out(multiplexer_4_out), .sel(or_6_out));
  or or_6 (or_6_out, and_1_out, LUP_PUP_out);
  or or_7 (SET_PC, RET, CALL, branchunit_1_branch_taken);
  or or_8 (or_8_out, CLR_out, or_6_out);
  assign X_IN = or_8_out ? multiplexer_4_out : 8'bz;  // Controlled_Buffer controlled_buffer_1
  or or_9 (INDIRECT_OP, CALL, MEM_OP_RW, LD_out, SET_PC);
  or or_10 (MEM_OP_DATA, MEM_OP_RW, LD_out);

  assign ALU_OP[2:0] = OPCODE[2:0];
  assign REGISTER_ID = OPCODE[3:0];
endmodule

module ALUUnaryOp (
  input  [3:0] OP,
  input  [7:0] X_OUT,
  input  [7:0] Y,
  output [7:0] X_IN
);

  wire decoder_1_out2, decoder_1_out3, decoder_1_out5, or_1_out;
  wire [7:0] lshrsh_1_result, not_1_out;

  Decoder #(.select(3)) decoder_1 (
    .out2(decoder_1_out2), .out3(decoder_1_out3), .out5(decoder_1_out5), .sel(OP[2:0]), .en(OP[3]));  // open: out0, out1, out4, out6, out7
  or or_1 (or_1_out, decoder_1_out3, decoder_1_out2);
  LSHRSH lshrsh_1 (.LeftOrRight(decoder_1_out3), .A(X_OUT), .RESULT(lshrsh_1_result));
  assign not_1_out = ~X_OUT;  // NOT_Gate not_1, 8 bits wide
  assign X_IN = or_1_out ? lshrsh_1_result : 8'bz;  // Controlled_Buffer controlled_buffer_1
  assign X_IN = decoder_1_out5 ? not_1_out : 8'bz;  // Controlled_Buffer controlled_buffer_2

  // Notes on the sheet:
  //   000 - Add
  //   001 - Sub
  //   011 - Lsh
  //   010 - Rsh
  //   100 - XOR
  //   101 - NOT
  //   110 - AND
  //   111 - OR
endmodule

module ALUBinaryOp (
  input  [3:0] OP,
  input  [7:0] X_OUT,
  input  [7:0] Y,
  output [7:0] X_IN
);

  wire decoder_1_out4, decoder_1_out6, decoder_1_out7;
  wire [7:0] and_1_out, or_1_out, xor_1_out;

  Decoder #(.select(3)) decoder_1 (
    .out4(decoder_1_out4), .out6(decoder_1_out6), .out7(decoder_1_out7), .sel(OP[2:0]), .en(OP[3]));  // open: out0, out1, out2, out3, out5
  assign xor_1_out = X_OUT ^ Y;  // XOR_Gate xor_1, 8 bits wide
  assign and_1_out = X_OUT & Y;  // AND_Gate and_1, 8 bits wide
  assign or_1_out = X_OUT | Y;  // OR_Gate or_1, 8 bits wide
  assign X_IN = decoder_1_out4 ? xor_1_out : 8'bz;  // Controlled_Buffer controlled_buffer_1
  assign X_IN = decoder_1_out6 ? and_1_out : 8'bz;  // Controlled_Buffer controlled_buffer_2
  assign X_IN = decoder_1_out7 ? or_1_out : 8'bz;  // Controlled_Buffer controlled_buffer_3

  // Notes on the sheet:
  //   000 - Add
  //   001 - Sub
  //   011 - Lsh
  //   010 - Rsh
  //   100 - XOR
  //   101 - NOT
  //   110 - AND
  //   111 - OR
endmodule

module ALUAddSub (
  input  [3:0] OP,
  input  [7:0] X_OUT,
  input  [7:0] Y,
  output [7:0] X_IN
);

  wire decoder_1_out0, decoder_1_out1, or_1_out;
  wire [7:0] addsub_1_result;

  Decoder #(.select(3)) decoder_1 (
    .out0(decoder_1_out0), .out1(decoder_1_out1), .sel(OP[2:0]), .en(OP[3]));  // open: out2, out3, out4, out5, out6, out7
  or or_1 (or_1_out, decoder_1_out1, decoder_1_out0);
  AddSub addsub_1 (.A(X_OUT), .ControlAddSub(decoder_1_out1), .B(Y), .RESULT(addsub_1_result));
  assign X_IN = or_1_out ? addsub_1_result : 8'bz;  // Controlled_Buffer controlled_buffer_1

  // Notes on the sheet:
  //   000 - Add
  //   001 - Sub
  //   011 - Lsh
  //   010 - Rsh
  //   100 - XOR
  //   101 - NOT
  //   110 - AND
  //   111 - OR
endmodule
